// Logisim project reg(2-add).circ as structural Verilog: 8 circuits, main circuit main
module main (
  input  in_1,
  input  [15:0] in_2,
  input  in_3,
  input  enable,
  input  enable_2,
  output [15:0] out_6,
  output ODD_Parity,
  output EVEN_Parity,
  output Zero,
  output Sign,
  output Half_Carry,
  output Carry,
  output Overflow,
  output Borrow
);

  wire and_1_out, clock_1_out, not_1_out, not_2_out, or_1_out, shift_register_1_out, shift_register_1_q0,
       shift_register_1_q1, shift_register_1_q3, shift_register_2_out;
  wire [3:0] ALU, multiplexer_2_out;
  wire [15:0] demultiplexer_1_out0, demultiplexer_1_out1, MAR_q, MBR_q, multiplexer_1_out, pc_1_data_out, Ra,
       Rb, rom_1_data, RZ_HiGH_q, RZ_LOW_q;
  wire [31:0] O_P;

  Shift_Register #(.length(6)) shift_register_1 (
    .shift(enable), .in(shift_register_1_out), .clk(clock_1_out), .out(shift_register_1_out),
    .q0(shift_register_1_q0), .q1(shift_register_1_q1), .q3(shift_register_1_q3));  // open: load, clr, d0, d1, d2, q2, d3, d4, q4, d5, q5
  PC pc_1 (
    .DATA_IN(in_2), .PC_enable(shift_register_1_out), .CLOCK(clock_1_out), .DATA_OUT(pc_1_data_out),
    .Reset(in_3));
  Register #(.width(16)) MAR (.D(pc_1_data_out), .en(shift_register_1_out), .Q(MAR_q), .clk(clock_1_out));  // open: clr
  or or_1 (or_1_out, shift_register_1_q1, shift_register_1_q3);
  Shift_Register #(.length(6)) shift_register_2 (
    .shift(enable_2), .in(shift_register_2_out), .clk(clock_1_out), .out(shift_register_2_out));  // open: load, clr, d0, q0, d1, q1, d2, q2, d3, q3, d4, q4, d5, q5
  ROM #(.addrWidth(16), .dataWidth(16)) rom_1 (.addr(MAR_q), .data(rom_1_data));  // open: sel
  Register #(.width(16)) MBR (
    .D(rom_1_data), .en(shift_register_2_out), .Q({MBR_q[15:12], ALU, MBR_q[7:0]}), .clk(clock_1_out));  // open: clr
  Clock clock_1 (.out(clock_1_out));
  not not_1 (not_1_out, shift_register_1_q3);
  Multiplexer #(.width(16), .disabled(0), .enable("false")) multiplexer_1 (
    .in0(RZ_LOW_q), .in1(RZ_HiGH_q), .out(multiplexer_1_out), .sel(in_1));
  Multiplexer #(.width(4), .disabled(0), .enable("false")) multiplexer_2 (
    .in0(MBR_q[3:0]), .in1(MBR_q[7:4]), .out(multiplexer_2_out), .sel(and_1_out));
  and and_1 (and_1_out, not_2_out, or_1_out);
  not not_2 (not_2_out, shift_register_1_q0);
  register register_1 (
    .REGISTER(multiplexer_1_out), .clock(clock_1_out), .Rx(multiplexer_2_out), .R_W_prime(not_1_out),
    .Data_Out(out_6));
  Demultiplexer #(.width(16), .disabled(0), .enable("false")) demultiplexer_1 (
    .out0(demultiplexer_1_out0), .out1(demultiplexer_1_out1), .in(out_6), .sel(and_1_out));
  Hex_Digit_Display hex_digit_display_1 (.value(O_P[15:12]));  // open: dp
  Register #(.width(16)) u_RA (
    .D(demultiplexer_1_out0), .en(shift_register_1_q0), .Q(Ra), .clk(clock_1_out));  // open: clr
  Register #(.width(16)) u_RB (.D(demultiplexer_1_out1), .en(or_1_out), .Q(Rb), .clk(clock_1_out));  // open: clr
  Hex_Digit_Display hex_digit_display_2 (.value(O_P[11:8]));  // open: dp
  Hex_Digit_Display hex_digit_display_3 (.value(O_P[7:4]));  // open: dp
  ALU alu_1 (.REGISTER(Ra), .MEMORY(Rb), .ALU(ALU), .O_P(O_P));
  Hex_Digit_Display hex_digit_display_4 (.value(O_P[3:0]));  // open: dp
  Register #(.width(16)) RZ_LOW (.D(O_P[15:0]), .Q(RZ_LOW_q), .clk(clock_1_out));  // open: en, clr
  Register #(.width(16)) RZ_HiGH (.D(O_P[31:16]), .Q(RZ_HiGH_q), .clk(clock_1_out));  // open: en, clr
  PSW psw_1 (
    .INPUT(O_P), .OP_2(Rb), .OP_1(Ra), .ALU(ALU), .ODD_PARITY(ODD_Parity), .EVEN_PARITY(EVEN_Parity),
    .ZERO(Zero), .SIGN_BIT(Sign), .Half_Carry(Half_Carry), .Overflow(Carry), .Carry(Overflow), .Borrow(Borrow));

  // Notes on the sheet:
  //   contents of rom_1 (hex, n*v repeats v):
  //   210 201 10 7875*0 212 44641*0 201 7877*0 21f
endmodule

module register (
  input  [15:0] REGISTER,
  input  clock,
  input  [3:0] Rx,
  input  R_W_prime,
  output [15:0] Data_Out
);

  wire decoder_1_out0, decoder_1_out1, decoder_1_out2, decoder_1_out3, decoder_1_out4, decoder_1_out5,
       decoder_1_out6, decoder_1_out7, decoder_1_out8, decoder_1_out9, decoder_1_out10, decoder_1_out11,
       decoder_1_out12, decoder_1_out13, decoder_1_out14, not_1_out;
  wire [15:0] R0_q, R1_q, R2_q, R3_q, R4_q, R5_q, R6_q, R7_q, R8_q, R9_q, R10_q, R11_q, R12_q, R13_q, R14_q,
       R15_q;

  not not_1 (not_1_out, R_W_prime);
  Decoder #(.select(4), .disabled(0)) decoder_1 (
    .out0(decoder_1_out0), .out1(decoder_1_out1), .out2(decoder_1_out2), .out3(decoder_1_out3),
    .out4(decoder_1_out4), .out5(decoder_1_out5), .out6(decoder_1_out6), .out7(decoder_1_out7),
    .out8(decoder_1_out8), .out9(decoder_1_out9), .out10(decoder_1_out10), .out11(decoder_1_out11),
    .out12(decoder_1_out12), .out13(decoder_1_out13), .out14(decoder_1_out14), .out15(decoder_1_out13),
    .sel(Rx), .en(not_1_out));
  Register #(.width(16)) R0 (.D(REGISTER), .en(decoder_1_out0), .Q(R0_q), .clk(clock));  // open: clr
  Register #(.width(16)) R1 (.D(REGISTER), .en(decoder_1_out1), .Q(R1_q), .clk(clock));  // open: clr
  Register #(.width(16)) R2 (.D(REGISTER), .en(decoder_1_out2), .Q(R2_q), .clk(clock));  // open: clr
  Register #(.width(16)) R3 (.D(REGISTER), .en(decoder_1_out3), .Q(R3_q), .clk(clock));  // open: clr
  Register #(.width(16)) R4 (.D(REGISTER), .en(decoder_1_out4), .Q(R4_q), .clk(clock));  // open: clr
  Register #(.width(16)) R5 (.D(REGISTER), .en(decoder_1_out5), .Q(R5_q), .clk(clock));  // open: clr
  Register #(.width(16)) R6 (.D(REGISTER), .en(decoder_1_out6), .Q(R6_q), .clk(clock));  // open: clr
  Register #(.width(16)) R7 (.D(REGISTER), .en(decoder_1_out7), .Q(R7_q), .clk(clock));  // open: clr
  Register #(.width(16)) R8 (.D(REGISTER), .en(decoder_1_out8), .Q(R8_q), .clk(clock));  // open: clr
  Register #(.width(16)) R9 (.D(REGISTER), .en(decoder_1_out9), .Q(R9_q), .clk(clock));  // open: clr
  Register #(.width(16)) R10 (.D(REGISTER), .en(decoder_1_out10), .Q(R10_q), .clk(clock));  // open: clr
  Register #(.width(16)) R11 (.D(REGISTER), .en(decoder_1_out11), .Q(R11_q), .clk(clock));  // open: clr
  Register #(.width(16)) R12 (.D(REGISTER), .en(decoder_1_out12), .Q(R12_q), .clk(clock));  // open: clr
  Register #(.width(16)) R13 (.D(REGISTER), .en(decoder_1_out13), .Q(R13_q), .clk(clock));  // open: clr
  Register #(.width(16)) R14 (.D(REGISTER), .en(decoder_1_out14), .Q(R14_q), .clk(clock));  // open: clr
  Register #(.width(16)) R15 (.D(REGISTER), .en(decoder_1_out13), .Q(R15_q), .clk(clock));  // open: clr
  Multiplexer #(.select(4), .width(16), .disabled(0)) multiplexer_1 (
    .in0(R0_q), .in1(R1_q), .in2(R2_q), .in3(R3_q), .in4(R4_q), .in5(R5_q), .in6(R6_q), .in7(R7_q),
    .in8(R8_q), .in9(R9_q), .in10(R10_q), .in11(R11_q), .in12(R12_q), .in13(R13_q), .in14(R14_q),
    .in15(R15_q), .out(Data_Out), .sel(Rx), .en(R_W_prime));
endmodule

module PC (
  input  [15:0] DATA_IN,
  input  PC_enable,
  input  Reset,
  input  CLOCK,
  output [15:0] DATA_OUT
);

  wire [15:0] adder_1_out;

  Adder #(.width(16)) adder_1 (.a(DATA_OUT), .b(DATA_IN), .out(adder_1_out), .cin(1'b1));  // open: cout
  Register #(.width(16)) register_1 (.D(adder_1_out), .en(PC_enable), .Q(DATA_OUT), .clk(CLOCK), .clr(Reset));
endmodule

module ALU (
  input  [15:0] REGISTER,
  input  [15:0] MEMORY,
  input  [3:0] ALU,
  output [31:0] O_P
);

  wire adder_1_cout, adder_2_cout, subtractor_1_bout, subtractor_2_bout;
  wire [3:0] bit_extender_3_out, bit_extender_4_out, bit_extender_5_out, bit_extender_6_out;
  wire [15:0] adder_1_out, adder_2_out, and_1_out, bit_extender_9_out, bit_extender_10_out,
       bit_extender_11_out, bit_extender_12_out, divider_1_out, divider_1_rem, multiplier_1_cout,
       multiplier_1_out, not_1_out, or_1_out, shifter_1_out, shifter_2_out, shifter_3_out, shifter_4_out,
       subtractor_1_out, subtractor_2_out;
  wire [31:0] adder_3_out, bit_extender_1_out, bit_extender_2_out, bit_extender_7_out, bit_extender_8_out,
       bit_extender_13_out, bit_extender_14_out, bit_extender_15_out, bit_extender_16_out,
       bit_extender_17_out, bit_extender_18_out, bit_extender_19_out, shifter_5_out, shifter_6_out;

  Adder #(.width(16)) adder_1 (.a(REGISTER), .b(MEMORY), .out(adder_1_out), .cout(adder_1_cout));  // open: cin
  Subtractor #(.width(16)) subtractor_1 (
    .a(REGISTER), .b(MEMORY), .out(subtractor_1_out), .bout(subtractor_1_bout));  // open: bin
  Multiplier #(.width(16)) multiplier_1 (
    .a(REGISTER), .b(MEMORY), .out(multiplier_1_out), .cout(multiplier_1_cout));  // open: cin
  Divider #(.width(16)) divider_1 (.a(REGISTER), .b(MEMORY), .out(divider_1_out), .rem(divider_1_rem));  // open: upper
  Adder #(.width(16)) adder_2 (.a(REGISTER), .b(16'h1), .out(adder_2_out), .cout(adder_2_cout));  // open: cin
  Subtractor #(.width(16)) subtractor_2 (
    .a(REGISTER), .b(16'h1), .out(subtractor_2_out), .bout(subtractor_2_bout));  // open: bin
  assign and_1_out = REGISTER & MEMORY;  // AND_Gate and_1, 16 bits wide
  assign or_1_out = REGISTER | MEMORY;  // OR_Gate or_1, 16 bits wide
  assign not_1_out = ~REGISTER;  // NOT_Gate not_1, 16 bits wide
  assign bit_extender_1_out = {{16{1'b0}}, REGISTER};  // Bit_Extender bit_extender_1
  assign bit_extender_2_out = {{16{1'b0}}, MEMORY};  // Bit_Extender bit_extender_2
  Bit_Extender #(.in_width(16), .out_width(4)) bit_extender_3 (.in(MEMORY), .out(bit_extender_3_out));
  Bit_Extender #(.in_width(16), .out_width(4)) bit_extender_4 (.in(MEMORY), .out(bit_extender_4_out));
  Bit_Extender #(.in_width(16), .out_width(4)) bit_extender_5 (.in(MEMORY), .out(bit_extender_5_out));
  Bit_Extender #(.in_width(16), .out_width(4)) bit_extender_6 (.in(MEMORY), .out(bit_extender_6_out));
  assign bit_extender_7_out = {{16{1'b0}}, MEMORY};  // Bit_Extender bit_extender_7
  assign bit_extender_8_out = {{16{1'b0}}, REGISTER};  // Bit_Extender bit_extender_8
  Shifter #(.width(16), .shift("lr")) shifter_1 (.in(REGISTER), .\dist (bit_extender_3_out), .out(shifter_1_out));
  Shifter #(.width(16)) shifter_2 (.in(REGISTER), .\dist (bit_extender_4_out), .out(shifter_2_out));
  Shifter #(.width(16), .shift("rr")) shifter_3 (.in(REGISTER), .\dist (bit_extender_5_out), .out(shifter_3_out));
  Shifter #(.width(16), .shift("rl")) shifter_4 (.in(REGISTER), .\dist (bit_extender_6_out), .out(shifter_4_out));
  Shifter #(.width(32)) shifter_5 (.in(bit_extender_8_out), .\dist (5'b10000), .out(shifter_5_out));
  assign bit_extender_9_out = {{15{1'b0}}, adder_1_cout};  // Bit_Extender bit_extender_9
  assign bit_extender_10_out = {{15{1'b0}}, subtractor_1_bout};  // Bit_Extender bit_extender_10
  assign bit_extender_11_out = {{15{1'b0}}, adder_2_cout};  // Bit_Extender bit_extender_11
  assign bit_extender_12_out = {{15{1'b0}}, subtractor_2_bout};  // Bit_Extender bit_extender_12
  assign bit_extender_13_out = {{16{1'b0}}, and_1_out};  // Bit_Extender bit_extender_13
  assign bit_extender_14_out = {{16{1'b0}}, or_1_out};  // Bit_Extender bit_extender_14
  assign bit_extender_15_out = {{16{1'b0}}, not_1_out};  // Bit_Extender bit_extender_15
  Shifter #(.width(32)) shifter_6 (.in(bit_extender_1_out), .\dist (5'b10000), .out(shifter_6_out));
  Adder #(.width(32)) adder_3 (.a(shifter_6_out), .b(bit_extender_2_out), .out(adder_3_out));  // open: cin, cout
  assign bit_extender_16_out = {{16{1'b0}}, shifter_1_out};  // Bit_Extender bit_extender_16
  assign bit_extender_17_out = {{16{1'b0}}, shifter_2_out};  // Bit_Extender bit_extender_17
  assign bit_extender_18_out = {{16{1'b0}}, shifter_3_out};  // Bit_Extender bit_extender_18
  assign bit_extender_19_out = {{16{1'b0}}, shifter_4_out};  // Bit_Extender bit_extender_19
  Multiplexer #(.select(4), .width(32), .disabled(0), .enable("false")) multiplexer_1 (
    .in0(bit_extender_7_out), .in1(shifter_5_out), .in2({bit_extender_9_out, adder_1_out}),
    .in3({bit_extender_10_out, subtractor_1_out}), .in4({multiplier_1_cout, multiplier_1_out}),
    .in5({divider_1_rem, divider_1_out}), .in6({bit_extender_11_out, adder_2_out}),
    .in7({bit_extender_12_out, subtractor_2_out}), .in8(bit_extender_13_out), .in9(bit_extender_14_out),
    .in10(bit_extender_15_out), .in11(adder_3_out), .in12(bit_extender_16_out), .in13(bit_extender_17_out),
    .in14(bit_extender_18_out), .in15(bit_extender_19_out), .out(O_P), .sel(ALU));

  // Notes on the sheet:
  //   ALU
  //   0000-LOAD
  //   0001-STORE
  //   0010-ADD
  //   0011-SUB
  //   0100-MULTIPLY
  //   0101-DEVIDE
  //   0110-INCREMENT
  //   0111-DECREMENT
  //   1000-AND
  //   1001-OR
  //   1010-NOT
  //   1011-EXCHANGE
  //   1100-SHIFT RIGHT
  //   1101-SHIFT LEFT
  //   1110-ROTATE RIGHT
  //   1111-ROTATE LEFT
endmodule

module delay_circuit (
  input  enable,
  input  clock,
  output \output ,
  output _4,
  output _5
);

  Shift_Register #(.length(5)) shift_register_1 (
    .shift(enable), .in(\output ), .clk(clock), .out(\output ), .q0(_5), .q1(_4));  // open: load, clr, d0, d1, d2, q2, d3, q3, d4, q4
endmodule

module register_delay (
  input  enable,
  input  clock,
  output \output 
);

  Shift_Register #(.length(4)) shift_register_1 (
    .shift(enable), .in(\output ), .clk(clock), .out(\output ));  // open: load, clr, d0, q0, d1, q1, d2, q2, d3, q3
endmodule

module R_W__of_reg (
  input  enable,
  input  clock,
  output \output 
);

  Shift_Register #(.length(4)) shift_register_1 (
    .shift(enable), .in(\output ), .clk(clock), .out(\output ));  // open: load, clr, d0, q0, d1, q1, d2, q2, d3, q3
endmodule

module PSW (
  input  [31:0] INPUT,
  input  [15:0] OP_2,
  input  [15:0] OP_1,
  input  [3:0] ALU,
  output ODD_PARITY,
  output EVEN_PARITY,
  output ZERO,
  output SIGN_BIT,
  output Half_Carry,
  output Overflow,
  output Carry,
  output Borrow
);

  wire [31:0] alu_1_o_p;

  Comparator #(.width(32)) comparator_1 (.a(INPUT), .b({32{1'b0}}), .eq(ZERO));  // open: gt, lt
  xor odd_parity_1 (ODD_PARITY, INPUT[0], INPUT[1], INPUT[2], INPUT[3], INPUT[4], INPUT[5], INPUT[6], INPUT[7], INPUT[8], INPUT[9], INPUT[10], INPUT[11], INPUT[12], INPUT[13], INPUT[14], INPUT[15], INPUT[17], INPUT[18], INPUT[19], INPUT[20], INPUT[21], INPUT[22], INPUT[23], INPUT[24], INPUT[25], INPUT[26], INPUT[27], INPUT[28], INPUT[29], INPUT[30], INPUT[31], INPUT[16]);
  xnor even_parity_1 (EVEN_PARITY, INPUT[0], INPUT[1], INPUT[2], INPUT[3], INPUT[4], INPUT[5], INPUT[6], INPUT[7], INPUT[8], INPUT[9], INPUT[10], INPUT[11], INPUT[12], INPUT[13], INPUT[14], INPUT[15], INPUT[17], INPUT[18], INPUT[19], INPUT[20], INPUT[21], INPUT[22], INPUT[23], INPUT[24], INPUT[25], INPUT[26], INPUT[27], INPUT[28], INPUT[29], INPUT[30], INPUT[31], INPUT[16]);
  Adder adder_1 (.a(OP_2[7:0]), .b(OP_1[7:0]), .cout(Half_Carry));  // open: out, cin
  ALU alu_1 (.REGISTER(OP_2), .MEMORY(OP_1), .ALU(ALU), .O_P(alu_1_o_p));
  Adder #(.width(16)) adder_2 (.a(OP_1), .b(OP_2), .cout(Carry));  // open: out, cin
  Subtractor #(.width(16)) subtractor_1 (.a(OP_1), .b(OP_2), .bout(Borrow));  // open: out, bin
  Comparator #(.width(16)) comparator_2 (.a(alu_1_o_p[31:16]), .b({16{1'b0}}), .gt(Overflow));  // open: eq, lt

  assign SIGN_BIT = INPUT[31];

  // Notes on the sheet:
  //   ZERO
endmodule
